# Fritzing sketch test (saved by Fritzing 0.9.3b)
breadboards: 1

parts:
  R1 = Resistor [tolerance=±5% resistance=220 package=THT]
  R2 = Resistor [tolerance=±5% resistance=220 package=THT]
  R3 = Resistor [tolerance=±5% resistance=220 package=THT]
  R4 = Resistor [tolerance=±5% resistance=220 package=THT]
  R5 = Resistor [tolerance=±5% resistance=220 package=THT]
  R6 = Resistor [tolerance=±5% resistance=220 package=THT]
  R8 = Resistor [tolerance=±5% resistance=220 package=THT]
  R9 = Resistor [tolerance=±5% resistance=220 package=THT]
  R10 = Resistor [tolerance=±5% resistance=220 package=THT]
  R11 = Resistor [tolerance=±5% resistance=220 package=THT]
  Composant1 = Arduino Uno (Rev3)
  LED1 = LED - 5mm [color="Red (633nm)" package="5 mm [THT]"]
  LED2 = LED - 5mm [color="Red (633nm)" package="5 mm [THT]"]
  LED3 = LED - 5mm [color="Red (633nm)" package="5 mm [THT]"]
  LED4 = LED - 5mm [color="Red (633nm)" package="5 mm [THT]"]
  LED5 = LED - 5mm [color="Red (633nm)" package="5 mm [THT]"]
  LED6 = LED - 5mm [color="Red (633nm)" package="5 mm [THT]"]
  LED7 = LED - 5mm [color="Red (633nm)" package="5 mm [THT]"]
  LED8 = LED - 5mm [color="Red (633nm)" package="5 mm [THT]"]
  LED9 = LED - 5mm [color="Red (633nm)" package="5 mm [THT]"]
  LED10 = LED - 5mm [color="Red (633nm)" package="5 mm [THT]"]

nets:
  N1: R1.Pin_0, LED1.cathode
  N2: R1.Pin_1, R2.Pin_1, R3.Pin_1, R4.Pin_1, R5.Pin_1, R6.Pin_1, R8.Pin_1, R9.Pin_1, R10.Pin_1, R11.Pin_1, Composant1.GND
  N3: R2.Pin_0, LED2.cathode
  N4: R3.Pin_0, LED4.cathode
  N5: R4.Pin_0, LED7.cathode
  N6: R5.Pin_0, LED5.cathode
  N7: R6.Pin_0, LED3.cathode
  N8: R8.Pin_0, LED8.cathode
  N9: R9.Pin_0, LED9.cathode
  N10: R10.Pin_0, LED10.cathode
  N11: R11.Pin_0, LED6.cathode
  N12: Composant1.D8, LED9.anode
  N13: Composant1.D9_PWM, LED7.anode
  N14: Composant1.D10_PWM/SS, LED5.anode
  N15: Composant1.D11_PWM/MOSI, LED2.anode
  N16: Composant1.D12/MISO, LED4.anode
  N17: Composant1.D13/SCK, LED1.anode
  N18: Composant1.D4, LED8.anode
  N19: Composant1.D5_PWM, LED6.anode
  N20: Composant1.D6_PWM, LED10.anode
  N21: Composant1.D7, LED3.anode
